// Digital circuit All32Bits0.dig as structural Verilog
module All32Bits0 (
  input  [31:0] Input,
  output All32Bits0
);

  xnor xnor_1 (All32Bits0, Input[0], Input[1], Input[2], Input[3], Input[4], Input[5], Input[6], Input[7], Input[8], Input[9], Input[10], Input[11], Input[12], Input[13], Input[14], Input[15], Input[16], Input[17], Input[18], Input[19], Input[20], Input[21], Input[22], Input[23], Input[24], Input[25], Input[26], Input[27], Input[28], Input[29], Input[30], Input[31], 1'b0);
endmodule
