// Digital circuit InstructionDecoder.dig as structural Verilog
// The InstructionDecoder component, which serves as a hub to control many of the signals to other components. It implements both the fetch operation, and execution of machine code (including decoding).
module InstructionDecoder (
  input  [31:0] Instruction,
  input  Fetch,
  input  Execute,
  input  [31:0] SP,
  output [3:0] Condition,
  output Halt,
  output [3:0] Reg_dest,
  output [3:0] Reg_B,
  output [3:0] Reg_A,
  output [2:0] Opcode,
  output nRE,
  output nWE,
  output [31:0] Constant,
  output SetFlags,
  output UseConstant,
  output PUSH,
  output POP,
  output LOADHI,
  output ARITHMETIC,
  output [2:0] _31bitnREnWE,
  output [31:0] SPafterPUSH
);

  wire add_1_s, all6bits1_3_p2, not_3_out, or_2_out, xnor_2_out, xnor_3_out, xnor_4_out, xnor_5_out;
  wire [1:0] xnor_1_out;
  wire [31:0] bitextender_1_out, bitextender_2_out;

  xnor xnor_1 (xnor_1_out[0], 1'b1, Instruction[30]);
  xnor xnor_2 (xnor_2_out, 1'b0, Instruction[26]);
  xnor xnor_3 (xnor_3_out, 1'b1, Instruction[26]);
  xnor xnor_4 (xnor_4_out, 1'b0, Instruction[26]);
  xnor xnor_5 (xnor_5_out, 1'b0, Instruction[26]);
  not not_1 (ARITHMETIC, Instruction[31]);
  and and_1 (LOADHI, xnor_1_out[0], xnor_1_out[1]);
  // All6Bits1 all6bits1_1: pin names not known; wires that end beside it: xnor_2_out, POP
  // All6Bits1 all6bits1_2: pin names not known; wires that end beside it: xnor_4_out, _31bitnREnWE[2]
  // All6Bits1 all6bits1_3: pin names not known; wires that end beside it: xnor_5_out, all6bits1_3_p2
  or or_1 (_31bitnREnWE[1], POP, all6bits1_3_p2);
  AllBits1 allbits1_1 (.Instruction_NoCond(Instruction[31:4]), .AllBits1(Halt));
  // All6Bits1 all6bits1_4: pin names not known; wires that end beside it: xnor_3_out, PUSH
  or or_2 (or_2_out, xnor_3_out, _31bitnREnWE[2]);
  not not_2 (nRE, _31bitnREnWE[1]);
  not not_3 (not_3_out, Instruction[26]);
  not not_4 (nWE, or_2_out);
  BitExtender #(.inputBits(10), .outputBits(32)) bitextender_1 (.in(Instruction[25:16]), .out(bitextender_1_out));
  or or_3 (UseConstant, not_3_out, _31bitnREnWE[1], _31bitnREnWE[2]);
  BitExtender #(.inputBits(22), .outputBits(32)) bitextender_2 (.in(Instruction[29:8]), .out(bitextender_2_out));
  Add add_1 (.a(1'b0), .b(SP[0]), .c_i(1'b0), .s(add_1_s));  // open: c_o
  Multiplexer multiplexer_1 (.sel(PUSH), .in_0(SP[0]), .in_1(add_1_s), .out(SPafterPUSH[0]));
  Multiplexer #(.Selector_Bits(2), .Bits(32)) multiplexer_2 (
    .sel(Instruction[31:30]), .in_0(bitextender_2_out), .in_1(bitextender_2_out), .in_2(bitextender_1_out),
    .in_3(bitextender_2_out), .out(Constant));
  // Pins of 1 and 6 bits meet at Instruction[31:26]
  // Pins of 1 and 6 bits meet at 6'b110000
  // Pins of 1 and 6 bits meet at 6'b111000
  // Pins of 1 and 6 bits meet at 6'b110001
  // Pins of 1 and 6 bits meet at 6'b110100
  // Pins of 1 and 2 bits meet at 2'b01
  // Pins of 1 and 2 bits meet at Instruction[31:30]
  // Pins of 1 and 2 bits meet at xnor_1_out
  // Pins of 1 and 32 bits meet at SPafterPUSH
  // Pins of 1 and 6 bits meet at 6'b111100
  // Pins of 1 and 32 bits meet at SP

  assign _31bitnREnWE[0] = Instruction[31];
  assign Condition = Instruction[3:0];
  assign Opcode = Instruction[30:28];
  assign Reg_A = Instruction[15:12];
  assign Reg_B = Instruction[11:8];
  assign Reg_dest = Instruction[7:4];
  assign SetFlags = Instruction[27];

  // Notes on the sheet:
  //   Instruction: The instruction machine code input. If the CPU is in the fetch phase and a rising clock signal occurs, this machine code is stored in the internal instruction register (IR), so that it can be decoded and executed.
  //   Condition: Instruction condition output, which contains the condition under which the instruction should be executed.
  //   Reg_dest: Destination register output, which determines the register that should store the result of a data operation. A data operation is either an ALU computation, or a read from an external device, such as RAM.
  //   Reg_B: B register output, which determines the register to be used for the second operand.
  //   Reg_A: A register output, which determines the register to be used for the first operand.
  //   Opcode: Opcode output, which determines the operation the ALU should perform.
endmodule
